# Fritzing sketch P1 (saved by Fritzing 0.9.1b)
breadboards: 1

parts:
  Part1 = Arduino Uno (Rev3)
  LED1 = LED - 5mm [color="Red (633nm)" package="5 mm [THT]"]
  LED2 = LED - 5mm [color="Red (633nm)" package="5 mm [THT]"]
  R1 = Resistor [package="0402 [SMD]"]
  R2 = Resistor [package="0402 [SMD]"]
  Part3 = Bluetooth Mate Silver
  VCC1 = Battery  # not connected
  VCC2 = Battery  # not connected
  IR1 = TSOP312.., 314.. [package=THT]

nets:
  N1: Part1.A0, IR1.Data
  N2: Part1.D13/SCK, R1.Pin_1
  N3: Part1.D0/RX, Part3.TX_5V
  N4: Part1.D1/TX, Part3.RX_5V
  N5: Part1.D5_PWM, R2.Pin_1
  3V3: Part1.3V3, Part3.VCC
  N6: Part1.5V, IR1.Vs
  GND: Part1.GND, LED1.cathode, LED2.cathode, Part3.GND, IR1.GND
  N7: LED1.anode, R1.Pin_0
  N8: LED2.anode, R2.Pin_0
