# Fritzing sketch P2 (saved by Fritzing 0.9.1b)
breadboards: 1

parts:
  LED1 = LED - 5mm [color="Red (633nm)" package="5 mm [THT]"]
  LED2 = LED - 5mm [color="Red (633nm)" package="5 mm [THT]"]
  R1 = Resistor [package="0402 [SMD]"]
  R2 = Resistor [package="0402 [SMD]"]
  Part3 = Bluetooth Mate Silver
  IR1 = TSOP312.., 314.. [package=THT]
  Part4 = Arduino Nano (Rev3.0)
  BAT1 = Battery Holders [package=battcon_12mm]

nets:
  GND: LED1.cathode, LED2.cathode, Part3.GND, IR1.GND
  N1: LED1.anode, R1.Pin_0
  N2: LED2.anode, R2.Pin_0
  N3: Part3.RX_5V, Part4.D1/TX
  N4: Part3.TX_5V, Part4.D0/RX
  VCC: Part3.VCC, Part4.3V3
  N5: IR1.Vs, Part4.5V
  N6: IR1.Data, Part4.A0
  N7: Part4.GND, BAT1.-
  N8: Part4.VIN, BAT1.+
